# Fritzing sketch sketch (saved by Fritzing 0.9.3b)
breadboards: 1

parts:
  Part1 = Arduino Uno (Rev3)
  R2 = Resistor [tolerance=±1% resistance=5.1k package=THT]
  R1 = Resistor [tolerance=±1% resistance=200 package=THT]
  R3 = Rotary Potentiometer (Small) [maximum_resistance=100kΩ package=THT]
  DS1 = DS18B20 1-Wire Temperature Sensor [part_number=DS18B20]
  U1 = LCD-16X2 [package=lcd-16x2]

nets:
  N1: Part1.D11_PWM/MOSI, U1.E
  N2: Part1.D12/MISO, U1.RS
  N3: Part1.D2, U1.DB7
  N4: Part1.D3_PWM, U1.DB6
  N5: Part1.D4, U1.DB5
  N6: Part1.D5_PWM, U1.DB4
  N7: Part1.D7, R2.Pin_1, DS1.DQ
  VDD: Part1.5V, R2.Pin_0, R1.Pin_0, R3.leg2, DS1.VDD, U1.VDD
  GND: Part1.GND, R3.leg1, DS1.GND, U1.VSS, U1.R_W, U1.K
  N8: R3.wiper, U1.VO
